# Fritzing sketch esp-nano-mqtt-IR-AC_controll (saved by Fritzing 0.9.3b)

parts:
  U1 = NodeMCU V1.0
  Part1 = Arduino Nano (Rev3.0)
  LED1 = RGB LED - (4 legs) [package="5 mm [THT]"]
  D1 = LTE-302 [package=lte-302]

nets:
  N1: U1.RX, Part1.D1/TX
  N2: U1.TX, Part1.D0/RX
  N3: Part1.GND, LED1.common_anode, D1.A
  N4: Part1.D3, D1.C
  N5: Part1.D7, LED1.red_cathode
  N6: Part1.D8, LED1.green_cathode
  N7: Part1.D9, LED1.blue_cathode

custom parts:
  NodeMCU V1.0: ESP8266 based NodeMCU
